// Logisim project ALU.circ as structural Verilog
module ALU (
  input  [31:0] A,
  input  [31:0] B,
  input  [1:0] ALUcontrol,
  output ZF,
  output NF,
  output [31:0] result,
  output CF,
  output OV
);

  wire adder_1_cout, not_2_out, xnor_1_out, xor_1_out;
  wire [31:0] adder_1_out, and_1_out, multiplexer_1_out, not_1_out, or_1_out;

  assign not_1_out = ~B;  // NOT_Gate not_1, 32 bits wide
  Multiplexer #(.width(32), .enable("false")) multiplexer_1 (
    .in0(B), .in1(not_1_out), .out(multiplexer_1_out), .sel(ALUcontrol[0]));
  Adder #(.width(32)) adder_1 (
    .a(A), .b(multiplexer_1_out), .out(adder_1_out), .cin(ALUcontrol[0]), .cout(adder_1_cout));
  assign and_1_out = A & B;  // AND_Gate and_1, 32 bits wide
  assign or_1_out = A | B;  // OR_Gate or_1, 32 bits wide
  not not_2 (not_2_out, ALUcontrol[1]);
  xor xor_1 (xor_1_out, adder_1_out[31], A[31]);
  NotExactlyOne xnor_1 (.out(xnor_1_out), .in0(A[31]), .in1(ALUcontrol[0]), .in2(B[31]));
  Multiplexer #(.select(2), .width(32), .enable("false")) multiplexer_2 (
    .in0(adder_1_out), .in1(adder_1_out), .in2(and_1_out), .in3(or_1_out), .out({NF, result[30:0]}),
    .sel(ALUcontrol));
  and and_2 (CF, adder_1_cout, not_2_out);
  and and_3 (OV, not_2_out, xor_1_out, xnor_1_out);
  ZeroFlag zeroflag_1 (.in({NF, result[30:0]}), .zf(ZF));

  assign result[31] = NF;
endmodule

module ZeroFlag (
  input  [31:0] in,
  output zf
);

  wire or_1_out;

  or or_1 (or_1_out, in[0], in[1], in[2], in[3], in[4], in[5], in[6], in[7], in[8], in[9], in[10], in[11], in[12], in[13], in[14], in[15], in[16], in[17], in[18], in[19], in[20], in[21], in[22], in[23], in[24], in[25], in[26], in[27], in[28], in[29], in[30], in[31]);
  not not_1 (zf, or_1_out);
endmodule
