// Logisim project MIPS.circ as structural Verilog: 10 circuits, main circuit main
module main (
);

  wire and_1_out, and_2_out, button_1_out, button_2_out, CLK, controlunit2_1_addiu, controlunit2_1_aluop0,
       controlunit2_1_aluop1, controlunit2_1_alusrc, controlunit2_1_beq, controlunit2_1_bne,
       controlunit2_1_jump, controlunit2_1_lb, controlunit2_1_lh, controlunit2_1_lu, controlunit2_1_memtoreg,
       controlunit2_1_memwrite, controlunit2_1_regdst, controlunit2_1_regwrite, or_1_out, zero_1_zf;
  wire [2:0] controlunit_1_aluctr;
  wire [4:0] multiplexer_2_out, splitter_1__15_11, splitter_1__20_16, splitter_1__25_21;
  wire [5:0] splitter_1__31_26;
  wire [15:0] splitter_1__15_0;
  wire [31:0] adder_1_out, adder_2_out, alu_1_out, extender_1_out, loadbytehw_1_out, multiplexer_1_out,
       multiplexer_3_out, multiplexer_4_out, ram32_1_rd, regfile32_1_rd1, regfile32_1_rd2, register_1_q,
       rom32_1_out_2, shifter_1_out;

  Clock clock_1 (.out(CLK));
  Multiplexer #(.width(32), .enable("false")) multiplexer_1 (
    .in0(adder_1_out), .in1(adder_2_out), .out(multiplexer_1_out), .sel(or_1_out));
  Register #(.width(32)) register_1 (
    .D(multiplexer_1_out), .Q(register_1_q), .clk(CLK), .clr(button_1_out));  // open: en
  Button button_1 (.out(button_1_out));
  Adder #(.width(32)) adder_1 (.a(register_1_q), .b(32'h4), .out(adder_1_out));  // open: cin, cout
  ROM32 rom32_1 (.A(register_1_q), .out_2(rom32_1_out_2));
  Splitter splitter_1 (
    .Instr(rom32_1_out_2), ._31_26(splitter_1__31_26), ._25_21(splitter_1__25_21),
    ._20_16(splitter_1__20_16), ._15_0(splitter_1__15_0), ._15_11(splitter_1__15_11));  // open: _5_0
  ControlUnit2 controlunit2_1 (
    .in_1(splitter_1__31_26), .BEQ(controlunit2_1_beq), .BNE(controlunit2_1_bne),
    .MemtoReg(controlunit2_1_memtoreg), .LB(controlunit2_1_lb), .LH(controlunit2_1_lh),
    .LU(controlunit2_1_lu), .MemWrite(controlunit2_1_memwrite), .ALUsrc(controlunit2_1_alusrc),
    .RegDst(controlunit2_1_regdst), .Jump(controlunit2_1_jump), .ADDIU(controlunit2_1_addiu),
    .RegWrite(controlunit2_1_regwrite), .Aluop1(controlunit2_1_aluop1), .Aluop0(controlunit2_1_aluop0));
  Button button_2 (.out(button_2_out));
  RegFile32 regfile32_1 (
    .A1(splitter_1__25_21), .A2(splitter_1__20_16), .A3(multiplexer_2_out), .WD(multiplexer_4_out),
    .RST(button_2_out), .WE(controlunit2_1_regwrite), .CLK(CLK), .RD1(regfile32_1_rd1), .RD2(regfile32_1_rd2));
  Multiplexer #(.width(5), .enable("false")) multiplexer_2 (
    .in0(splitter_1__20_16), .in1(splitter_1__15_11), .out(multiplexer_2_out), .sel(controlunit2_1_regdst));
  Extender extender_1 (
    ._0_15(splitter_1__15_0), ._16_20(splitter_1__20_16), ._21_25(splitter_1__25_21),
    .ADDIU(controlunit2_1_addiu), .Jump(controlunit2_1_jump), .out(extender_1_out));
  Multiplexer #(.width(32), .enable("false")) multiplexer_3 (
    .in0(regfile32_1_rd2), .in1(extender_1_out), .out(multiplexer_3_out), .sel(controlunit2_1_alusrc));
  ControlUnit controlunit_1 (
    .ALUop1(controlunit2_1_aluop1), .ALUop0(controlunit2_1_aluop0), .func(splitter_1__15_0[5:0]),
    .Aluctr(controlunit_1_aluctr));
  Shifter #(.width(32)) shifter_1 (.in(extender_1_out), .\dist (5'b00010), .out(shifter_1_out));
  ZERO zero_1 (.in(alu_1_out), .zf(zero_1_zf));
  ALU alu_1 (.A(regfile32_1_rd1), .B(multiplexer_3_out), .ALUctr(controlunit_1_aluctr), .out(alu_1_out));  // open: cout
  Adder #(.width(32)) adder_2 (.a(shifter_1_out), .b(adder_1_out), .out(adder_2_out));  // open: cin, cout
  and and_1 (and_1_out, zero_1_zf, controlunit2_1_beq);
  or or_1 (or_1_out, and_1_out, and_2_out);
  and and_2 (and_2_out, ~zero_1_zf, controlunit2_1_bne);  // AND_Gate
  RAM32 ram32_1 (.A(alu_1_out), .WD(regfile32_1_rd2), .clk(CLK), .MemWrite(controlunit2_1_memwrite), .RD(ram32_1_rd));
  LoadByteHw loadbytehw_1 (
    .in_3(ram32_1_rd), .LU(controlunit2_1_lu), .LH(controlunit2_1_lh), .LB(controlunit2_1_lb),
    .out(loadbytehw_1_out));
  Multiplexer #(.width(32), .enable("false")) multiplexer_4 (
    .in0(alu_1_out), .in1(loadbytehw_1_out), .out(multiplexer_4_out), .sel(controlunit2_1_memtoreg));

  // Notes on the sheet:
  //   LB 10 0000
  //   LH 10 0001
  //   LW 10 0011
  //   LBU 10 0100
  //   LHU 10 0101
  //   SW 10 1011
  //   TODO ADDIU, opt lb/lh
  //   ADD, ADDI, ADDIU, SUB, AND, OR, SLT, LW, SW, LB, LBU, LH, LHU, BEQ, BNE, J
endmodule

module ControlUnit (
  input  ALUop1,
  input  ALUop0,
  input  [5:0] func,
  output [2:0] Aluctr
);

  wire and_1_out, and_2_out, and_3_out, and_4_out, and_5_out, and_6_out, and_7_out, and_8_out, and_9_out,
       and_10_out, and_11_out, and_12_out, and_13_out, and_14_out, and_15_out, and_16_out, and_17_out,
       and_18_out, and_19_out, not_1_out, not_2_out, not_3_out, not_4_out, not_5_out, not_6_out, not_7_out,
       not_8_out, not_9_out, not_10_out, not_11_out, not_12_out, or_1_out, or_2_out, or_3_out, or_4_out,
       or_5_out, or_6_out, or_7_out, or_9_out;

  not not_1 (not_1_out, ALUop1);
  not not_2 (not_2_out, func[0]);
  not not_3 (not_3_out, func[3]);
  not not_4 (not_4_out, ALUop1);
  not not_5 (not_5_out, func[0]);
  not not_6 (not_6_out, func[1]);
  not not_7 (not_7_out, func[2]);
  not not_8 (not_8_out, func[4]);
  not not_9 (not_9_out, func[1]);
  not not_10 (not_10_out, func[3]);
  and and_1 (and_1_out, not_1_out, ALUop0);
  and and_2 (and_2_out, ALUop1, not_2_out);
  and and_3 (and_3_out, ALUop1, not_3_out);
  and and_4 (and_4_out, ALUop1, func[4]);
  and and_5 (and_5_out, ALUop1, func[2]);
  or or_1 (or_1_out, not_4_out, not_5_out);
  not not_11 (not_11_out, func[3]);
  or or_2 (or_2_out, func[4], func[2]);
  and and_6 (and_6_out, ALUop1, func[0]);
  and and_7 (and_7_out, not_6_out, not_7_out);
  and and_8 (and_8_out, func[3], not_8_out);
  and and_9 (and_9_out, ALUop1, func[0]);
  and and_10 (and_10_out, not_9_out, func[2]);
  and and_11 (and_11_out, not_10_out, func[4]);
  not not_12 (not_12_out, func[5]);
  or or_3 (or_3_out, and_1_out, and_2_out);
  and and_12 (and_12_out, and_3_out, func[5]);
  or or_4 (or_4_out, and_4_out, and_5_out);
  and and_13 (and_13_out, ALUop1, func[1]);
  or or_5 (or_5_out, or_1_out, not_11_out);
  or or_6 (or_6_out, or_2_out, func[1]);
  and and_14 (and_14_out, and_6_out, and_7_out);
  and and_15 (and_15_out, and_8_out, func[5]);
  and and_16 (and_16_out, and_9_out, and_10_out);
  and and_17 (and_17_out, and_11_out, not_12_out);
  or or_7 (or_7_out, or_3_out, and_12_out);
  or or_8 (Aluctr[2], or_7_out, or_9_out);
  or or_9 (or_9_out, or_4_out, and_13_out);
  or or_10 (Aluctr[1], or_5_out, or_6_out);
  and and_18 (and_18_out, and_14_out, and_15_out);
  or or_11 (Aluctr[0], and_18_out, and_19_out);
  and and_19 (and_19_out, and_16_out, and_17_out);
endmodule

module ControlUnit1 (
  input  opcode5,
  input  opcode4,
  input  opcode3,
  input  opcode2,
  input  opcode1,
  input  opcode0,
  output BEQ,
  output BNE,
  output MemtoReg,
  output LB,
  output LH,
  output LU,
  output MemWrite,
  output ALUsrc,
  output RegDst,
  output Jump,
  output ADDIU,
  output RegWrite,
  output ALUop1,
  output ALUop0
);

  wire and_1_out, and_2_out, and_3_out, and_6_out, and_7_out, and_8_out, and_9_out, and_10_out, and_11_out,
       and_12_out, and_18_out, and_19_out, not_1_out, not_2_out, not_3_out, not_4_out, not_5_out, not_6_out,
       not_7_out, not_8_out, not_9_out, not_10_out, not_11_out;

  not not_1 (not_1_out, opcode5);
  not not_2 (not_2_out, opcode4);
  not not_3 (not_3_out, opcode3);
  not not_4 (not_4_out, opcode2);
  not not_5 (not_5_out, opcode0);
  not not_6 (not_6_out, opcode5);
  not not_7 (not_7_out, opcode4);
  not not_8 (not_8_out, opcode3);
  not not_9 (not_9_out, opcode2);
  not not_10 (not_10_out, opcode1);
  not not_11 (not_11_out, opcode0);
  and and_1 (and_1_out, ~opcode5, ~opcode4, ~opcode3, ~opcode2, ~opcode1, ~opcode0);  // AND_Gate
  and and_2 (and_2_out, opcode5, ~opcode4, ~opcode3, ~opcode2, opcode1, opcode0);  // AND_Gate
  and and_3 (and_3_out, ~opcode5, ~opcode4, opcode3, ~opcode2, ~opcode1, ~opcode0);  // AND_Gate
  and and_4 (ADDIU, ~opcode5, ~opcode4, opcode3, ~opcode2, ~opcode1, opcode0);  // AND_Gate
  and and_5 (RegDst, not_1_out, not_2_out, not_3_out, not_4_out, not_5_out);
  and and_6 (and_6_out, opcode5, ~opcode4, opcode3, ~opcode2, opcode1, opcode0);  // AND_Gate
  and and_7 (and_7_out, opcode5, ~opcode4, ~opcode3, ~opcode2, opcode1, opcode0);  // AND_Gate
  and and_8 (and_8_out, opcode5, ~opcode4, ~opcode3, ~opcode2, ~opcode1, ~opcode0);  // AND_Gate
  and and_9 (and_9_out, opcode5, ~opcode4, ~opcode3, opcode2, ~opcode1, ~opcode0);  // AND_Gate
  and and_10 (and_10_out, opcode5, ~opcode4, ~opcode3, ~opcode2, ~opcode1, opcode0);  // AND_Gate
  and and_11 (and_11_out, opcode5, ~opcode4, ~opcode3, opcode2, ~opcode1, opcode0);  // AND_Gate
  and and_12 (and_12_out, ~opcode5, ~opcode4, opcode3, ~opcode2, ~opcode1, ~opcode0);  // AND_Gate
  and and_13 (BEQ, ~opcode5, ~opcode4, ~opcode3, opcode2, ~opcode1, ~opcode0);  // AND_Gate
  and and_14 (BNE, ~opcode5, ~opcode4, ~opcode3, opcode2, ~opcode1, opcode0);  // AND_Gate
  and and_15 (MemWrite, opcode5, ~opcode4, opcode3, ~opcode2, opcode1, opcode0);  // AND_Gate
  and and_16 (Jump, ~opcode5, ~opcode4, ~opcode3, ~opcode2, opcode1, ~opcode0);  // AND_Gate
  and and_17 (ALUop1, not_6_out, not_7_out, not_8_out, not_9_out, not_10_out, not_11_out);
  and and_18 (and_18_out, ~opcode5, ~opcode4, ~opcode3, opcode2, ~opcode1, ~opcode0);  // AND_Gate
  and and_19 (and_19_out, ~opcode5, ~opcode4, ~opcode3, opcode2, ~opcode1, opcode0);  // AND_Gate
  or or_1 (RegWrite, and_1_out, and_2_out, and_3_out, ADDIU);
  or or_2 (ALUop0, and_18_out, and_19_out);
  or or_3 (ALUsrc, and_6_out, and_7_out, and_8_out, and_9_out, BNE, and_11_out, and_12_out, ADDIU);
  or or_4 (MemtoReg, and_7_out, and_8_out, and_9_out, and_10_out, and_11_out);
  or or_5 (LB, and_8_out, and_9_out);
  or or_6 (LU, and_9_out, and_11_out);
  or or_7 (LH, and_10_out, and_11_out);

  // Other names for the same wires on the sheet: regW = RegWrite
endmodule

// CONTROL
module ControlUnit2 (
  input  [5:0] in_1,
  output BEQ,
  output BNE,
  output MemtoReg,
  output LB,
  output LH,
  output LU,
  output MemWrite,
  output ALUsrc,
  output RegDst,
  output Jump,
  output ADDIU,
  output RegWrite,
  output Aluop1,
  output Aluop0
);

  ControlUnit1 controlunit1_1 (
    .opcode5(in_1[5]), .opcode4(in_1[4]), .opcode3(in_1[3]), .opcode2(in_1[2]), .opcode1(in_1[1]),
    .opcode0(in_1[0]), .BEQ(BEQ), .BNE(BNE), .MemtoReg(MemtoReg), .LB(LB), .LH(LH), .LU(LU),
    .MemWrite(MemWrite), .ALUsrc(ALUsrc), .RegDst(RegDst), .Jump(Jump), .ADDIU(ADDIU), .RegWrite(RegWrite),
    .ALUop1(Aluop1), .ALUop0(Aluop0));
endmodule

module ALU (
  input  [31:0] A,
  input  [31:0] B,
  input  [2:0] ALUctr,
  output [31:0] out,
  output cout
);

  wire [31:0] adder_1_out, and_1_out, bit_extender_1_out, multiplexer_1_out, not_1_out, or_1_out;

  Multiplexer #(.width(32), .enable("false")) multiplexer_1 (
    .in0(B), .in1(not_1_out), .out(multiplexer_1_out), .sel(ALUctr[2]));
  assign not_1_out = ~B;  // NOT_Gate not_1, 32 bits wide
  assign and_1_out = A & multiplexer_1_out;  // AND_Gate and_1, 32 bits wide
  assign or_1_out = A | multiplexer_1_out;  // OR_Gate or_1, 32 bits wide
  Adder #(.width(32)) adder_1 (.a(A), .b(multiplexer_1_out), .out(adder_1_out), .cout(cout));  // open: cin
  assign bit_extender_1_out = {{1{1'b0}}, adder_1_out[30:0]};  // Bit_Extender bit_extender_1
  Multiplexer #(.select(2), .width(32), .enable("false")) multiplexer_2 (
    .in0(and_1_out), .in1(or_1_out), .in2(adder_1_out), .in3(bit_extender_1_out), .out(out), .sel(ALUctr[1:0]));
endmodule

// REGFILE
module RegFile32 (
  input  [4:0] A1,
  input  RST,
  input  WE,
  input  CLK,
  input  [4:0] A2,
  input  [4:0] A3,
  input  [31:0] WD,
  output [31:0] RD1,
  output [31:0] RD2
);

  wire decoder_1_out0, decoder_1_out1, decoder_1_out2, decoder_1_out3, decoder_1_out4, decoder_1_out5,
       decoder_1_out6, decoder_1_out7, decoder_1_out8, decoder_1_out9, decoder_1_out10, decoder_1_out11,
       decoder_1_out12, decoder_1_out13, decoder_1_out14, decoder_1_out15, decoder_2_out0, decoder_2_out1,
       decoder_2_out2, decoder_2_out3, decoder_2_out4, decoder_2_out5, decoder_2_out6, decoder_2_out7,
       decoder_2_out8, decoder_2_out9, decoder_2_out10, decoder_2_out11, decoder_2_out12, decoder_2_out13,
       decoder_2_out14, decoder_2_out15, not_1_out;
  wire [31:0] a0_q, a1_q, a2_q, a3_q, at_q, controlled_buffer_1_out, controlled_buffer_2_out,
       controlled_buffer_3_out, controlled_buffer_4_out, controlled_buffer_5_out, controlled_buffer_6_out,
       controlled_buffer_7_out, controlled_buffer_8_out, controlled_buffer_9_out, controlled_buffer_10_out,
       controlled_buffer_11_out, controlled_buffer_12_out, controlled_buffer_13_out,
       controlled_buffer_14_out, controlled_buffer_15_out, controlled_buffer_16_out,
       controlled_buffer_17_out, controlled_buffer_18_out, controlled_buffer_19_out,
       controlled_buffer_20_out, controlled_buffer_21_out, controlled_buffer_22_out,
       controlled_buffer_23_out, controlled_buffer_24_out, controlled_buffer_25_out,
       controlled_buffer_26_out, controlled_buffer_27_out, controlled_buffer_28_out,
       controlled_buffer_29_out, controlled_buffer_30_out, controlled_buffer_31_out,
       controlled_buffer_32_out, fp_q, gp_q, k0_q, k1_q, multiplexer_1_out, multiplexer_2_out,
       multiplexer_3_out, multiplexer_4_out, ra_q, s0_q, s1_q, s2_q, s3_q, s4_q, s5_q, s6_q, s7_q, sp_q,
       t0_q, t1_q, t2_q, t3_q, t4_q, t5_q, t6_q, t7_q, t8_q, t9_q, v0_q, v1_q, zero_q;

  assign controlled_buffer_1_out = decoder_1_out0 ? WD : 32'bz;  // Controlled_Buffer controlled_buffer_1
  assign controlled_buffer_2_out = decoder_1_out1 ? WD : 32'bz;  // Controlled_Buffer controlled_buffer_2
  assign controlled_buffer_3_out = decoder_1_out2 ? WD : 32'bz;  // Controlled_Buffer controlled_buffer_3
  assign controlled_buffer_4_out = decoder_1_out3 ? WD : 32'bz;  // Controlled_Buffer controlled_buffer_4
  assign controlled_buffer_5_out = decoder_1_out4 ? WD : 32'bz;  // Controlled_Buffer controlled_buffer_5
  Decoder #(.select(4)) decoder_1 (
    .out0(decoder_1_out0), .out1(decoder_1_out1), .out2(decoder_1_out2), .out3(decoder_1_out3),
    .out4(decoder_1_out4), .out5(decoder_1_out5), .out6(decoder_1_out6), .out7(decoder_1_out7),
    .out8(decoder_1_out8), .out9(decoder_1_out9), .out10(decoder_1_out10), .out11(decoder_1_out11),
    .out12(decoder_1_out12), .out13(decoder_1_out13), .out14(decoder_1_out14), .out15(decoder_1_out15),
    .sel(A3[3:0]), .en(not_1_out));
  not not_1 (not_1_out, A3[4]);
  assign controlled_buffer_6_out = decoder_2_out0 ? WD : 32'bz;  // Controlled_Buffer controlled_buffer_6
  assign controlled_buffer_7_out = decoder_2_out1 ? WD : 32'bz;  // Controlled_Buffer controlled_buffer_7
  assign controlled_buffer_8_out = decoder_2_out2 ? WD : 32'bz;  // Controlled_Buffer controlled_buffer_8
  assign controlled_buffer_9_out = decoder_2_out3 ? WD : 32'bz;  // Controlled_Buffer controlled_buffer_9
  Decoder #(.select(4)) decoder_2 (
    .out0(decoder_2_out0), .out1(decoder_2_out1), .out2(decoder_2_out2), .out3(decoder_2_out3),
    .out4(decoder_2_out4), .out5(decoder_2_out5), .out6(decoder_2_out6), .out7(decoder_2_out7),
    .out8(decoder_2_out8), .out9(decoder_2_out9), .out10(decoder_2_out10), .out11(decoder_2_out11),
    .out12(decoder_2_out12), .out13(decoder_2_out13), .out14(decoder_2_out14), .out15(decoder_2_out15),
    .sel(A3[3:0]), .en(A3[4]));
  assign controlled_buffer_10_out = decoder_1_out5 ? WD : 32'bz;  // Controlled_Buffer controlled_buffer_10
  assign controlled_buffer_11_out = decoder_1_out6 ? WD : 32'bz;  // Controlled_Buffer controlled_buffer_11
  assign controlled_buffer_12_out = decoder_1_out7 ? WD : 32'bz;  // Controlled_Buffer controlled_buffer_12
  assign controlled_buffer_13_out = decoder_1_out8 ? WD : 32'bz;  // Controlled_Buffer controlled_buffer_13
  assign controlled_buffer_14_out = decoder_2_out4 ? WD : 32'bz;  // Controlled_Buffer controlled_buffer_14
  assign controlled_buffer_15_out = decoder_2_out5 ? WD : 32'bz;  // Controlled_Buffer controlled_buffer_15
  assign controlled_buffer_16_out = decoder_2_out6 ? WD : 32'bz;  // Controlled_Buffer controlled_buffer_16
  assign controlled_buffer_17_out = decoder_2_out7 ? WD : 32'bz;  // Controlled_Buffer controlled_buffer_17
  assign controlled_buffer_18_out = decoder_1_out9 ? WD : 32'bz;  // Controlled_Buffer controlled_buffer_18
  assign controlled_buffer_19_out = decoder_1_out10 ? WD : 32'bz;  // Controlled_Buffer controlled_buffer_19
  assign controlled_buffer_20_out = decoder_1_out11 ? WD : 32'bz;  // Controlled_Buffer controlled_buffer_20
  assign controlled_buffer_21_out = decoder_1_out12 ? WD : 32'bz;  // Controlled_Buffer controlled_buffer_21
  assign controlled_buffer_22_out = decoder_2_out8 ? WD : 32'bz;  // Controlled_Buffer controlled_buffer_22
  assign controlled_buffer_23_out = decoder_2_out9 ? WD : 32'bz;  // Controlled_Buffer controlled_buffer_23
  assign controlled_buffer_24_out = decoder_2_out10 ? WD : 32'bz;  // Controlled_Buffer controlled_buffer_24
  assign controlled_buffer_25_out = decoder_2_out11 ? WD : 32'bz;  // Controlled_Buffer controlled_buffer_25
  assign controlled_buffer_26_out = decoder_1_out13 ? WD : 32'bz;  // Controlled_Buffer controlled_buffer_26
  assign controlled_buffer_27_out = decoder_1_out14 ? WD : 32'bz;  // Controlled_Buffer controlled_buffer_27
  assign controlled_buffer_28_out = decoder_1_out15 ? WD : 32'bz;  // Controlled_Buffer controlled_buffer_28
  assign controlled_buffer_29_out = decoder_2_out12 ? WD : 32'bz;  // Controlled_Buffer controlled_buffer_29
  assign controlled_buffer_30_out = decoder_2_out13 ? WD : 32'bz;  // Controlled_Buffer controlled_buffer_30
  assign controlled_buffer_31_out = decoder_2_out14 ? WD : 32'bz;  // Controlled_Buffer controlled_buffer_31
  assign controlled_buffer_32_out = decoder_2_out15 ? WD : 32'bz;  // Controlled_Buffer controlled_buffer_32
  Register #(.width(32)) zero (.D(controlled_buffer_1_out), .en(WE), .Q(zero_q), .clk(CLK), .clr(RST));
  Register #(.width(32)) at (.D(controlled_buffer_2_out), .en(WE), .Q(at_q), .clk(CLK), .clr(RST));
  Register #(.width(32)) v0 (.D(controlled_buffer_3_out), .en(WE), .Q(v0_q), .clk(CLK), .clr(RST));
  Register #(.width(32)) v1 (.D(controlled_buffer_4_out), .en(WE), .Q(v1_q), .clk(CLK), .clr(RST));
  Register #(.width(32)) a0 (.D(controlled_buffer_5_out), .en(WE), .Q(a0_q), .clk(CLK), .clr(RST));
  Register #(.width(32)) u_a1 (.D(controlled_buffer_10_out), .en(WE), .Q(a1_q), .clk(CLK), .clr(RST));
  Register #(.width(32)) u_a2 (.D(controlled_buffer_11_out), .en(WE), .Q(a2_q), .clk(CLK), .clr(RST));
  Register #(.width(32)) u_a3 (.D(controlled_buffer_12_out), .en(WE), .Q(a3_q), .clk(CLK), .clr(RST));
  Register #(.width(32)) t0 (.D(controlled_buffer_13_out), .en(WE), .Q(t0_q), .clk(CLK), .clr(RST));
  Register #(.width(32)) t1 (.D(controlled_buffer_18_out), .en(WE), .Q(t1_q), .clk(CLK), .clr(RST));
  Register #(.width(32)) t2 (.D(controlled_buffer_19_out), .en(WE), .Q(t2_q), .clk(CLK), .clr(RST));
  Register #(.width(32)) t3 (.D(controlled_buffer_20_out), .en(WE), .Q(t3_q), .clk(CLK), .clr(RST));
  Register #(.width(32)) t4 (.D(controlled_buffer_21_out), .en(WE), .Q(t4_q), .clk(CLK), .clr(RST));
  Register #(.width(32)) t5 (.D(controlled_buffer_26_out), .en(WE), .Q(t5_q), .clk(CLK), .clr(RST));
  Register #(.width(32)) t6 (.D(controlled_buffer_27_out), .en(WE), .Q(t6_q), .clk(CLK), .clr(RST));
  Register #(.width(32)) t7 (.D(controlled_buffer_28_out), .en(WE), .Q(t7_q), .clk(CLK), .clr(RST));
  Register #(.width(32)) s0 (.D(controlled_buffer_6_out), .en(WE), .Q(s0_q), .clk(CLK), .clr(RST));
  Register #(.width(32)) s1 (.D(controlled_buffer_7_out), .en(WE), .Q(s1_q), .clk(CLK), .clr(RST));
  Register #(.width(32)) s2 (.D(controlled_buffer_8_out), .en(WE), .Q(s2_q), .clk(CLK), .clr(RST));
  Register #(.width(32)) s3 (.D(controlled_buffer_9_out), .en(WE), .Q(s3_q), .clk(CLK), .clr(RST));
  Register #(.width(32)) s4 (.D(controlled_buffer_14_out), .en(WE), .Q(s4_q), .clk(CLK), .clr(RST));
  Register #(.width(32)) s5 (.D(controlled_buffer_15_out), .en(WE), .Q(s5_q), .clk(CLK), .clr(RST));
  Register #(.width(32)) s6 (.D(controlled_buffer_16_out), .en(WE), .Q(s6_q), .clk(CLK), .clr(RST));
  Register #(.width(32)) s7 (.D(controlled_buffer_17_out), .en(WE), .Q(s7_q), .clk(CLK), .clr(RST));
  Register #(.width(32)) t8 (.D(controlled_buffer_22_out), .en(WE), .Q(t8_q), .clk(CLK), .clr(RST));
  Register #(.width(32)) t9 (.D(controlled_buffer_23_out), .en(WE), .Q(t9_q), .clk(CLK), .clr(RST));
  Register #(.width(32)) k0 (.D(controlled_buffer_24_out), .en(WE), .Q(k0_q), .clk(CLK), .clr(RST));
  Register #(.width(32)) k1 (.D(controlled_buffer_25_out), .en(WE), .Q(k1_q), .clk(CLK), .clr(RST));
  Register #(.width(32)) gp (.D(controlled_buffer_29_out), .en(WE), .Q(gp_q), .clk(CLK), .clr(RST));
  Register #(.width(32)) sp (.D(controlled_buffer_30_out), .en(WE), .Q(sp_q), .clk(CLK), .clr(RST));
  Register #(.width(32)) fp (.D(controlled_buffer_31_out), .en(WE), .Q(fp_q), .clk(CLK), .clr(RST));
  Register #(.width(32)) ra (.D(controlled_buffer_32_out), .en(WE), .Q(ra_q), .clk(CLK), .clr(RST));
  Multiplexer #(.select(4), .width(32)) multiplexer_1 (
    .in0(zero_q), .in1(at_q), .in2(v0_q), .in3(v1_q), .in4(a0_q), .in5(a1_q), .in6(a2_q), .in7(a3_q),
    .in8(t0_q), .in9(t1_q), .in10(t2_q), .in11(t3_q), .in12(t4_q), .in13(t5_q), .in14(t6_q), .in15(t7_q),
    .out(multiplexer_1_out), .sel(A1[3:0]));  // open: en
  Multiplexer #(.select(4), .width(32)) multiplexer_2 (
    .in0(zero_q), .in1(at_q), .in2(v0_q), .in3(v1_q), .in4(a0_q), .in5(a1_q), .in6(a2_q), .in7(a3_q),
    .in8(t0_q), .in9(t1_q), .in10(t2_q), .in11(t3_q), .in12(t4_q), .in13(t5_q), .in14(t6_q), .in15(t7_q),
    .out(multiplexer_2_out), .sel(A2[3:0]));  // open: en
  Multiplexer #(.select(4), .width(32)) multiplexer_3 (
    .in0(s0_q), .in1(s1_q), .in2(s2_q), .in3(s3_q), .in4(s4_q), .in5(s5_q), .in6(s6_q), .in7(s7_q),
    .in8(t8_q), .in9(t9_q), .in10(k0_q), .in11(k1_q), .in12(gp_q), .in13(sp_q), .in14(fp_q), .in15(ra_q),
    .out(multiplexer_3_out), .sel(A1[3:0]));  // open: en
  Multiplexer #(.select(4), .width(32)) multiplexer_4 (
    .in0(s0_q), .in1(s1_q), .in2(s2_q), .in3(s3_q), .in4(s4_q), .in5(s5_q), .in6(s6_q), .in7(s7_q),
    .in8(t8_q), .in9(t9_q), .in10(k0_q), .in11(k1_q), .in12(gp_q), .in13(sp_q), .in14(fp_q), .in15(ra_q),
    .out(multiplexer_4_out), .sel(A2[3:0]));  // open: en
  Multiplexer #(.width(32), .enable("false")) multiplexer_5 (
    .in0(multiplexer_1_out), .in1(multiplexer_3_out), .out(RD1), .sel(A1[4]));
  Multiplexer #(.width(32), .enable("false")) multiplexer_6 (
    .in0(multiplexer_2_out), .in1(multiplexer_4_out), .out(RD2), .sel(A2[4]));
endmodule

module ZERO (
  input  [31:0] in,
  output zf
);

  wire or_1_out;

  or or_1 (or_1_out, in[0], in[1], in[2], in[3], in[4], in[5], in[6], in[7], in[8], in[9], in[10], in[11], in[12], in[13], in[14], in[15], in[16], in[17], in[18], in[19], in[20], in[21], in[22], in[23], in[24], in[25], in[26], in[27], in[28], in[29], in[30], in[31]);
  not not_1 (zf, or_1_out);
endmodule

// SPLITTER
module Splitter (
  input  [31:0] Instr,
  output [5:0] _31_26,
  output [5:0] _5_0,
  output [4:0] _25_21,
  output [4:0] _20_16,
  output [15:0] _15_0,
  output [4:0] _15_11
);


  assign _5_0 = Instr[5:0];
  assign _15_0 = Instr[15:0];
  assign _15_11 = Instr[15:11];
  assign _20_16 = Instr[20:16];
  assign _25_21 = Instr[25:21];
  assign _31_26 = Instr[31:26];
endmodule

module Extender (
  input  ADDIU,
  input  Jump,
  input  [15:0] _0_15,
  input  [4:0] _16_20,
  input  [4:0] _21_25,
  output [31:0] out
);

  wire [31:0] bit_extender_1_out, bit_extender_2_out, bit_extender_3_out, multiplexer_1_out;

  assign bit_extender_1_out = {{16{_0_15[15]}}, _0_15};  // Bit_Extender bit_extender_1
  assign bit_extender_2_out = {{16{1'b0}}, _0_15};  // Bit_Extender bit_extender_2
  assign bit_extender_3_out = {{6{_21_25[4]}}, {_21_25, _16_20, _0_15}};  // Bit_Extender bit_extender_3
  Multiplexer #(.width(32), .enable("false")) multiplexer_1 (
    .in0(bit_extender_1_out), .in1(bit_extender_2_out), .out(multiplexer_1_out), .sel(ADDIU));
  Multiplexer #(.width(32), .enable("false")) multiplexer_2 (
    .in0(multiplexer_1_out), .in1(bit_extender_3_out), .out(out), .sel(Jump));
endmodule

module LoadByteHw (
  input  LU,
  input  LH,
  input  [31:0] in_3,
  input  LB,
  output [31:0] out
);

  wire nor_1_out;
  wire [31:0] bit_extender_1_out, bit_extender_2_out, bit_extender_3_out, bit_extender_4_out,
       multiplexer_1_out, multiplexer_2_out;

  assign bit_extender_1_out = {{16{in_3[15]}}, in_3[15:0]};  // Bit_Extender bit_extender_1
  assign bit_extender_2_out = {{16{1'b0}}, in_3[15:0]};  // Bit_Extender bit_extender_2
  assign bit_extender_3_out = {{24{in_3[7]}}, in_3[7:0]};  // Bit_Extender bit_extender_3
  assign bit_extender_4_out = {{24{1'b0}}, in_3[7:0]};  // Bit_Extender bit_extender_4
  Multiplexer #(.width(32), .enable("false")) multiplexer_1 (
    .in0(bit_extender_1_out), .in1(bit_extender_2_out), .out(multiplexer_1_out), .sel(LU));
  assign out = LH ? multiplexer_1_out : 32'bz;  // Controlled_Buffer controlled_buffer_1
  assign out = LB ? multiplexer_2_out : 32'bz;  // Controlled_Buffer controlled_buffer_2
  Multiplexer #(.width(32), .enable("false")) multiplexer_2 (
    .in0(bit_extender_3_out), .in1(bit_extender_4_out), .out(multiplexer_2_out), .sel(LU));
  nor nor_1 (nor_1_out, LB, LH);
  assign out = nor_1_out ? in_3 : 32'bz;  // Controlled_Buffer controlled_buffer_3
endmodule
