// Logisim project Memory.circ as structural Verilog: 3 circuits, main circuit main
module main (
  input  [31:0] A,
  output [31:0] out_2
);

  ROM #(.addrWidth(6), .dataWidth(32)) rom_1 (.addr(A[7:2]), .data(out_2), .sel(1'b1));

  // Notes on the sheet:
  //   contents of rom_1 (hex, n*v repeats v):
  //   22 8c010000 8c020004 221822 1c600004 222020 8000002 24640000 1000ffff
endmodule

module ROM32 (
  input  [31:0] A,
  output [31:0] out_2
);

  ROM #(.addrWidth(6), .dataWidth(32)) rom_1 (.addr(A[7:2]), .data(out_2), .sel(1'b1));

  // Notes on the sheet:
  //   contents of rom_1 (hex, n*v repeats v):
  //   22 8c010000 8c020004 221822 1c600004 222020 8000002 24640000 1000ffff
endmodule

module RAM32 (
  input  clk,
  input  MemWrite,
  input  [31:0] A,
  input  [31:0] WD,
  output [31:0] RD
);

  wire not_1_out;

  not not_1 (not_1_out, MemWrite);
  RAM #(.addrWidth(6), .dataWidth(32), .bus("separate")) ram_1 (
    .addr(A[7:2]), .din(WD), .data(RD), .str(MemWrite), .sel(1'b1), .clk(clk), .ld(not_1_out));  // open: clr
endmodule
